# Fritzing sketch SCHEMA (saved by Fritzing 0.9.4)
perfboards: 1

parts:
  Punte_H_L298_/_Drive_Motoare = L298N DC motor driver
  Baterie_9V_/_Sursa_9V_DC = BC9VPC [package=bc9vpc]
  Motor_Dreapta = DC Motor
  Motor_Stanga = DC Motor
  HC-SR04_Sensor_1 = HC-SR04 Ultrasonic Distance Sensor  # not connected
  S1 = TCRT5000 [package=THT]  # not connected
  S2 = TCRT5000 [package=THT]  # not connected
  S3 = TCRT5000 [package=THT]  # not connected
  S4 = TCRT5000 [package=THT]  # not connected
  S5 = TCRT5000 [package=THT]  # not connected
  Near = TCRT5000 [package=THT]  # not connected
  Servo_Motor_Rotire_Senzor_US = Basic Servo  # not connected
  D2F2 = D2F-FL Omron Snap Action Limit Switch with Level  # not connected
  LCD2004-I2C1 = LCD2004-I2C  # not connected
  Bară_de_neopixeli_pentru_Semnalizare = WS2812 RGB LED matrix 1x8  # not connected
  Parte1 = Arduino Uno (Rev3)  # not connected

nets:
  N1: Punte_H_L298_/_Drive_Motoare.OUT1, Motor_Stanga.pin_2
  N2: Punte_H_L298_/_Drive_Motoare.OUT2, Motor_Stanga.pin_1
  N3: Punte_H_L298_/_Drive_Motoare.OUT3, Motor_Dreapta.pin_2
  N4: Punte_H_L298_/_Drive_Motoare.OUT4, Motor_Dreapta.pin_1
  N5: Punte_H_L298_/_Drive_Motoare.12V, Baterie_9V_/_Sursa_9V_DC.V+
  N6: Punte_H_L298_/_Drive_Motoare.GND, Baterie_9V_/_Sursa_9V_DC.V-

notes:
  Near
  CLP
  S5
  S4
  S3
  S2
  S1
  GND
  VCC
  Modul IR TCRT5000
  Mega 2560 Pin 20 SDA
  Mega 2560 Pin 21 SCL
  Comunicatie LCD Display I2C

custom parts:
  L298N DC motor driver: 2x DC motor driver with 78M05 positive voltage regulator (7..35 V) L298N: max 46 V, 2 A Set 5 V Enable jumper to enable 5 V regultor (needed for the L298N) and +5 V output at screw terminal or supply external +5 V at screw terminal Set ENA and/or ENB to +5 V to enable motor permanently or supply ENA and/or ENB with PWM signal IN1 and IN2 set rotation directory for motor A (OUT1/OUT2) IN2 and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
  TCRT5000: TCRT5000 optical reflective sensor
  D2F-FL Omron Snap Action Limit Switch with Level: Snap action switch with stainless steel lever.
  LCD2004-I2C: A standard character display with 4x20 characters. Comes in many colors with LCM2004 IIC attached.
  WS2812 RGB LED matrix 1x8: WS2812 matrix 1x8
